# Fritzing sketch IoT_MinecraftServer (saved by Fritzing 0.9.3b)
breadboards: 1

parts:
  Nokia_5110_LCD_Module1 = Nokia 5110 LCD
  U1 = LuaNode32 / ESP32

nets:
  VCC: Nokia_5110_LCD_Module1.VCC, Nokia_5110_LCD_Module1.LED, U1.3V3
  GND: Nokia_5110_LCD_Module1.GND, U1.GND
  N1: Nokia_5110_LCD_Module1.SCE, U1.TX2
  N2: Nokia_5110_LCD_Module1.RST, U1.RX2
  N3: Nokia_5110_LCD_Module1.D/C, U1.D4
  N4: Nokia_5110_LCD_Module1.DN(MOSI), U1.D2
  N5: Nokia_5110_LCD_Module1.SCLK, U1.D15

custom parts:
  Nokia 5110 LCD: Nokia 5110 Graphic 84*48 LCD module such as the Sparkfun LCD-10168 or the clones from Ebay. There is example code for the Arduino available from the Sparkfun site in https://learn.sparkfun.com/tutorials/graphic-lcd-hookup-guide This is a 3.3V device, if you are running it from a 5V micro you need a 5V tolorant level translator such as the 74ahc367 to protect the signal imputs. Rafa G. did a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
  LuaNode32 / ESP32: ESP32 based LuaNode32
